// Logisim project OneBitSummer.circ as structural Verilog: 1 circuit, main circuit main
module main (
  input  A,
  input  B,
  input  \С ,
  output S,
  output P
);

  wire not_1_out, not_2_out, not_3_out, or_1_out, or_2_out, or_3_out, or_4_out, or_5_out, or_6_out, or_7_out;

  not not_1 (not_1_out, A);
  not not_2 (not_2_out, B);
  not not_3 (not_3_out, \С );
  or or_1 (or_1_out, A, B, \С );
  or or_2 (or_2_out, A, not_2_out, not_3_out);
  or or_3 (or_3_out, not_1_out, B, not_3_out);
  or or_4 (or_4_out, not_1_out, not_2_out, \С );
  or or_5 (or_5_out, A, B);
  or or_6 (or_6_out, B, \С );
  or or_7 (or_7_out, A, \С );
  and and_1 (S, or_1_out, or_2_out, or_3_out, or_4_out);
  and and_2 (P, or_5_out, or_6_out, or_7_out);

  // Notes on the sheet:
  //   $
  //   B
  //   A
  //   С
  //   !A
  //   !B
  //   !С
endmodule
