// Logisim project DOWN_COUNTER_4bit.circ as structural Verilog: 1 circuit, main circuit main
module main (
  input  V
);

  wire clock_1_out, nand_1_out, nand_2_out, nand_3_out, nand_4_out, nand_5_out, or_1_out;
  wire [2:0] Q1_q;

  nand nand_1 (nand_1_out, 1'b1, or_1_out);
  nand nand_2 (nand_2_out, nand_3_out, 1'b1);
  or or_1 (or_1_out, nand_4_out, Q1_q[1], Q1_q[0]);
  nand nand_3 (nand_3_out, nand_5_out, V);
  nand nand_4 (nand_4_out, 1'b1, V);
  nand nand_5 (nand_5_out, Q1_q[0], 1'b1);
  Clock clock_1 (.out(clock_1_out));
  T_Flip_Flop Q3 (.clk(clock_1_out), .T(nand_1_out), .Q(Q1_q[2]));  // open: Qn, preset, reset
  T_Flip_Flop Q2 (.clk(clock_1_out), .T(nand_2_out), .Q(Q1_q[1]));  // open: Qn, preset, reset
  T_Flip_Flop Q1 (.clk(clock_1_out), .T(V), .Q(Q1_q[0]));  // open: Qn, preset, reset
  // Probe on Q1_q

  // Notes on the sheet:
  //   q3
  //   V
  //   q2
  //   q1
endmodule
